# Fritzing sketch ejemplo2_alarma_nodo_centralita (saved by Fritzing 0.9.3b)

parts:
  RFM95W2 = RFM95W LoRa Module
  U1 = keyestudio ESP32 plus development board [part_number=ESP32]
  RELAY1 = KS0011 Relay
  IC1 = KS0029 [chip_label=?]

nets:
  GND: RFM95W2.1_GND, U1.GND, RELAY1.GND, IC1.GND
  N1: RFM95W2.2_MISO, U1.io19
  N2: RFM95W2.3_MOSI, U1.io23
  N3: RFM95W2.4_SCK, U1.io18
  N4: RFM95W2.5_NSS_(CS), U1.io5
  N5: RFM95W2.6_RESET, U1.io13
  VCC: RFM95W2.13_3.3V, U1.5V, U1.VCC, RELAY1.VCC, IC1.VCC
  N6: RFM95W2.14_DIO0, U1.io12
  N7: U1.io25, IC1.S
  N8: U1.io17, RELAY1.S

custom parts:
  RFM95W LoRa Module: RF Transceiver by Hope RF. Well supported Arduino libraries are available. This Low Power Long Range Transceiver Module for the frequencies 868MHz and 915MHz and it is also available in other versions.
  keyestudio ESP32 plus development board: keyestudio ESP32 plus STEM makers development board 2.4GHz dual-mode WiFi + bluetooth dual cores microcontroller
  KS0029: Button
